# Fritzing sketch schematic (saved by Fritzing 1.0.2b)
breadboards: 1

parts:
  U1 = WS2812 RGB LED strip
  Mod1 = KY-018 Photoresistor Module [package="Breakout board"]
  Part1 = Arduino Uno (Rev3) - ICSP

nets:
  GND: U1.GND, Mod1.-, Part1.GND
  VCC: U1.VCC, Mod1.Vin, Part1.5V
  N1: U1.DIN, Part1.D8
  N2: Mod1.S, Part1.A0

custom parts:
  WS2812 RGB LED strip: WS2812 strip
  KY-018 Photoresistor Module: KY-018 Photoresistor module, used to measure light intensity. It can determine the presence or absence of light.
